# Fritzing sketch StratoStat_Bion_Space (saved by Fritzing 0.9.3b)

parts:
  LoRa_Module1 = Ra-01 - LoRa Module SX1278 [part_number=SX1278]
  Бортовой_вычислительный_модуль = Arduino Mega 2560 (Rev3)
  MPU6050 = GY-521 (MPU-6050) [form="♀ (female)" package=THT]
  RHT1 = Humidity and Temperature Sensor RHT03
  Часть1 = MicroSD Card Module
  Amperemeter1 = Amperemeter  # not connected
  Voltmeter1 = Voltmeter
  SENSOR1 = MPL115A2 Barometer Breakout Board
  VCC1 = Battery
  CAMERA1 = TTL Serial JPEG Camera

nets:
  GND: LoRa_Module1.GND, Бортовой_вычислительный_модуль.GND, MPU6050.pin2, RHT1.GND_1, Часть1.GND, Voltmeter1.Com, SENSOR1.GND, VCC1.-, CAMERA1.GND#5
  N1: LoRa_Module1.NSS, Бортовой_вычислительный_модуль.D10_PWM
  N2: LoRa_Module1.MOSI, Бортовой_вычислительный_модуль.D11_PWM
  N3: LoRa_Module1.MISO, Бортовой_вычислительный_модуль.D12_PWM
  N4: LoRa_Module1.SCK, Бортовой_вычислительный_модуль.D13_PWM
  3.3V: LoRa_Module1.3.3V, Бортовой_вычислительный_модуль.3V3, Voltmeter1.Positive
  N5: LoRa_Module1.DIO0, Бортовой_вычислительный_модуль.D2_PWM
  N6: Бортовой_вычислительный_модуль.A4, MPU6050.pin4
  N7: Бортовой_вычислительный_модуль.A5, MPU6050.pin3
  N8: Бортовой_вычислительный_модуль.A6, SENSOR1.SCL
  N9: Бортовой_вычислительный_модуль.A7, SENSOR1.SDA
  N10: Бортовой_вычислительный_модуль.IOREF, RHT1.Vcc
  N11: Бортовой_вычислительный_модуль.RESET, SENSOR1.RST
  5V: Бортовой_вычислительный_модуль.5V, MPU6050.pin1, Часть1.VCC, SENSOR1.VDD, CAMERA1.5V
  N12: Бортовой_вычислительный_модуль.VIN, VCC1.+
  N13: Бортовой_вычислительный_модуль.D0_RX0, CAMERA1.TX
  N14: Бортовой_вычислительный_модуль.D1_TX0, CAMERA1.RX
  N15: Бортовой_вычислительный_модуль.D22, RHT1.Data-signal
  N16: Бортовой_вычислительный_модуль.D50, Часть1.MISO
  N17: Бортовой_вычислительный_модуль.D51, Часть1.MOSI
  N18: Бортовой_вычислительный_модуль.D52, Часть1.SCK
  N19: Бортовой_вычислительный_модуль.D53, Часть1.CS

custom parts:
  Ra-01 - LoRa Module SX1278: The Ra-01 LoRa Module featuring the SX1278 engine by Semtech. Module by AI-Thinker. Module (Ra-01) specifications from: https://www.banggood.com/Ra-01-Smart-Electronics-SX1278-LoRa-Spread-Spectrum-Wireless-Module-Ultra-Far-10KM-433M-p-1130769.html Description: Power supply: DC1.8-3.7V(3.3V) Chip: SX1278 Frequency: 433Mhz Operating temperature: -40~+85°C On Sheild Description (may vary by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
  GY-521 (MPU-6050): Placa GY-521 basada en conjunto de acelerómetro+giroscopios MPU-6050
  Amperemeter: A Standard Multimeter in Current mode
  Voltmeter: A Standard Multimeter in Current mode
  MPL115A2 Barometer Breakout Board: MPL115A2 I2C Barometric Sensor
  TTL Serial JPEG Camera: TTL Serial JPEG Camera with NTSC Out
